// Logisim project Gray to Binary converter.circ as structural Verilog: 1 circuit, main circuit main
module main (
  input  in_1,
  input  in_2,
  input  in_3,
  input  in_4,
  output out_5,
  output out_6,
  output out_7,
  output out_8
);

  xor xor_1 (out_5, in_1, out_6);
  xor xor_2 (out_6, in_2, out_7);
  xor xor_3 (out_7, in_3, in_4);

  assign out_8 = in_4;
endmodule
