// Logisim project SMART STREET LIGHT.circ as structural Verilog: 1 circuit, main circuit main
module main (
  input  Light_sensor,
  input  Motion_sensor,
  input  Manual_switch,
  output Smart_Street_Light
);

  wire A_B_out, not_1_out;

  not not_1 (not_1_out, Light_sensor);
  and A_B (A_B_out, not_1_out, Motion_sensor);
  or A_B___C (Smart_Street_Light, A_B_out, Manual_switch);

  // Notes on the sheet:
  //   LIGHT SENSOR DID NOT DETECT LIGHT WHICH MEANS ITS DARK  AND MOTION IS DETECTED ----> THE STREET LIGHT IS ON 
endmodule
